# Fritzing sketch Solar_Station (saved by Fritzing 0.9.3b)
breadboards: 2

parts:
  Lolin_D1_Mini_v3_1 = WeMos D1 Mini
  WeMos_D1_Mini_Relay_Shield_V1 = WeMos D1 Mini Relay Shield V2
  TP4056_battery_charger_(protected) = TP4056 [chip_label=TP4056 package="DIP (Dual Inline) [THT]"]
  BAT1 = 18650 battery holder [package=battery-18650-kit]
  MT3608_DC_DC_step_up_to_5_5V = DC-DC 2-24V Step Up Booster [package=THT]
  5V_Solar_panel = Solar Cell
  1N4001_diode = Schottky Diode [part_number=1N5817 package="Melf DO-213 AB [SMD]"]
  3_5V-9V_3W_water_pump = DC Motor  # not connected
  R4 = Resistor [tolerance=±5% resistance=100k package="0603 [SMD]"]
  R3 = Resistor [tolerance=±5% resistance=220 package="0603 [SMD]"]
  22kΩ_+_4_7kΩ_in_series = Resistor [tolerance=±5% resistance=22k package="0603 [SMD]"]
  MT3608_DC_DC_step_up_to_8_66V = DC-DC 2-24V Step Up Booster [package=THT]
  Capacitive_Touch_Button_(TTP223) = IR Receiver Breakout [package=PCB]

nets:
  3V3: Lolin_D1_Mini_v3_1.3V3, Capacitive_Touch_Button_(TTP223).VCC
  N1: Lolin_D1_Mini_v3_1.5V, MT3608_DC_DC_step_up_to_5_5V.pin1
  N2: Lolin_D1_Mini_v3_1.A0, R4.Pin_1, 22kΩ_+_4_7kΩ_in_series.Pin_0
  N3: Lolin_D1_Mini_v3_1.D0, Lolin_D1_Mini_v3_1.RST, Capacitive_Touch_Button_(TTP223).OUT
  N4: Lolin_D1_Mini_v3_1.D5, WeMos_D1_Mini_Relay_Shield_V1.D5
  N5: Lolin_D1_Mini_v3_1.G, WeMos_D1_Mini_Relay_Shield_V1.G, MT3608_DC_DC_step_up_to_5_5V.pin2, Capacitive_Touch_Button_(TTP223).GND
  N6: TP4056_battery_charger_(protected).pin1, 1N4001_diode.cathode
  N7: TP4056_battery_charger_(protected).pin2, 5V_Solar_panel.-
  N8: TP4056_battery_charger_(protected).pin3, MT3608_DC_DC_step_up_to_5_5V.pin3
  N9: TP4056_battery_charger_(protected).pin4, BAT1.+, R3.Pin_1
  N10: TP4056_battery_charger_(protected).pin5, TP4056_battery_charger_(protected).pin6, BAT1.-, MT3608_DC_DC_step_up_to_5_5V.pin4, MT3608_DC_DC_step_up_to_8_66V.pin4
  N11: 5V_Solar_panel.+, 1N4001_diode.anode
  N12: R3.Pin_0, 22kΩ_+_4_7kΩ_in_series.Pin_1

notes:
  Solar Station
  by Davide Perini
  NOTE: GND of the battery MUST not be directly connected to the GND of the circuit.

custom parts:
  TP4056: A DIP stand-in part for whatever IC you want. With 6 pins on a 300mil dual inline package (DIP) footprint.
  18650 battery holder: 18650 Battery Holder
  DC-DC 2-24V Step Up Booster: Convertisseur DC-DC 2-24V 2A
